# Fritzing sketch wifi_回路図 (saved by Fritzing 0.9.5d)
circuit board: 6.09739cm x 5.22002cm
breadboards: 1

parts:
  Raspberry_Pi_1 = Raspberry Pi 3 [part_number=RPI-3-V1.2]
  M1 = DC Motor
  M2 = DC Motor
  C1 = Ceramic Capacitor [capacitance=100nF voltage=35V package="100 mil [THT, multilayer]"]
  パーツ1 = Triple Axis Magnetometer - HMC5883 Breakout
  IC1 = L293D [package=THT]
  VCC1 = 4 x AAA Battery Mount
  V1 = DC Power [voltage=3.3V]
  C2 = Ceramic Capacitor [capacitance=100nF voltage=35V package="100 mil [THT, multilayer]"]
  VCC2 = Battery block 9V
  C3 = Ceramic Capacitor [capacitance=100nF voltage=35V package="100 mil [THT, multilayer]"]

nets:
  N1: Raspberry_Pi_1.GPIO2, パーツ1.SCL
  N2: Raspberry_Pi_1.GPIO3, パーツ1.SDA
  N3: Raspberry_Pi_1.GIPO17, IC1.In_3
  N4: Raspberry_Pi_1.GIPO27, IC1.In_4
  N5: Raspberry_Pi_1.GIPO22, IC1.Enable_2
  N6: Raspberry_Pi_1.GIPO5, IC1.In_2
  N7: Raspberry_Pi_1.GIPO6, IC1.In_1
  N8: Raspberry_Pi_1.GIPO13, IC1.Enable_1
  GND: Raspberry_Pi_1.GND, C1.0, パーツ1.GND, IC1.0V, VCC1.-, V1.V-, C2.0, VCC2.-, C3.0
  N9: M1.pin_1, IC1.Out_3_(_Controlled_by_Enable_2_)
  N10: M1.pin_2, IC1.Out_4_(_Controlled_by_Enable_2_)
  N11: M2.pin_1, IC1.Out_2_(_Controlled_by_Enable_1_)
  N12: M2.pin_2, IC1.Out_1_(_Controlled_by_Enable_1_)
  vcc_5v: C1.1, IC1.+V, VCC1.+
  vcc_3_3: パーツ1.VCC
  vcc_9v: IC1.+Vmotor, VCC2.+, C3.1
  vcc_3v: V1.V+, C2.1
